# Fritzing sketch Schema (saved by Fritzing 0.9.3b)
circuit board: 21.3493cm x 13.3432cm
breadboards: 1

parts:
  Composant1 = Arduino Uno (Rev3)
  S1 = Pushbutton [package="[THT]"]
  S2 = Pushbutton [package="[THT]"]
  S3 = Pushbutton [package="[THT]"]
  S4 = Pushbutton [package="[THT]"]
  S5 = Pushbutton [package="[THT]"]
  S6 = Pushbutton [package="[THT]"]
  S7 = Pushbutton [package="[THT]"]
  Composant3 = Triple Axis Accelerometer Breakout - ADXL335

nets:
  N1: Composant1.A0, Composant3.XOUT
  N2: Composant1.A1, Composant3.YOUT
  N3: Composant1.A2, Composant3.ZOUT
  N4: Composant1.D8, S1.Pin_3
  GND: Composant1.GND, Composant1.D4, Composant1.D5_PWM, S1.Pin_1, S2.Pin_4, S3.Pin_1, S4.Pin_1, S5.Pin_1, S5.Pin_2, S5.Pin_3, S5.Pin_4, S6.Pin_3, S6.Pin_4, S7.Pin_1, S7.Pin_2, S7.Pin_3, S7.Pin_4, Composant3.GND
  N5: Composant1.D2, S2.Pin_2
  N6: Composant1.D3_PWM, S6.Pin_1, S6.Pin_2
  N7: Composant1.D6_PWM, S3.Pin_3
  N8: Composant1.D7, S4.Pin_3
  3V3: Composant1.3V3, Composant3.VCC
